# Fritzing sketch 温度设计电路 (saved by Fritzing 0.9.2b)
circuit board: 8.46667cm x 5.64444cm
breadboards: 1

parts:
  元件1 = Arduino Micro (Rev3)
  RHT1 = Humidity and Temperature Sensor RHT03

nets:
  N1: 元件1.GND, RHT1.GND_2
  5V: 元件1.5V, RHT1.Vcc
  N2: 元件1.A5, RHT1.Data-signal
